# Fritzing sketch Nano_DHT11_SDcard (saved by Fritzing 0.9.3b)
breadboards: 1

parts:
  DHT1 = DHT11 Humitidy and Temperature Sensor
  SD_card_module1 = SD Card Module
  Part1 = Arduino Nano (Rev3.0)

nets:
  N1: DHT1.VDD, SD_card_module1.+5
  N2: DHT1.DATA, Part1.D2
  N3: DHT1.GND, SD_card_module1.GND#7
  N4: SD_card_module1.CS, Part1.D10
  N5: SD_card_module1.MOSI, Part1.D11/MOSI
  N6: SD_card_module1.SCK, Part1.D13/SCK
  N7: SD_card_module1.MISO, Part1.D12/MISO

custom parts:
  DHT11 Humitidy and Temperature Sensor: DHT11 Humidity and Temperature Sensor
  SD Card Module: SD Card Module Slot Socket Reader For Arduino ARM MCU
